# Fritzing sketch Adjustable_Load_Schematic (saved by Fritzing 0.9.3b)

parts:
  R1 = Resistor [tolerance=±1% resistance=100 package=THT]
  SW1 = DIP SWITCH [package=dipswitch-02]
  R2 = Resistor [tolerance=±1% resistance=100 package=THT]
  R4 = Resistor [tolerance=±1% resistance=100 package=THT]
  SW2 = DIP SWITCH [package=dipswitch-02]
  R3 = Resistor [tolerance=±1% resistance=100 package=THT]
  R5 = Resistor [tolerance=±1% resistance=100 package=THT]
  SW3 = DIP SWITCH [package=dipswitch-02]
  R6 = Resistor [tolerance=±1% resistance=100 package=THT]
  SW4 = DIP SWITCH [package=dipswitch-02]
  R7 = Resistor [tolerance=±1% resistance=100 package=THT]
  R8 = Resistor [tolerance=±1% resistance=100 package=THT]
  R9 = Resistor [tolerance=±1% resistance=100 package=THT]
  SW5 = DIP SWITCH [package=dipswitch-02]
  R10 = Resistor [tolerance=±1% resistance=100 package=THT]
  R11 = Resistor [tolerance=±1% resistance=100 package=THT]
  R12 = Resistor [tolerance=±1% resistance=100 package=THT]
  SW6 = DIP SWITCH [package=dipswitch-02]
  SW7 = DIP SWITCH [package=dipswitch-02]
  R13 = Resistor [tolerance=±1% resistance=100 package=THT]
  R14 = Resistor [tolerance=±1% resistance=100 package=THT]
  R15 = Resistor [tolerance=±1% resistance=100 package=THT]
  SW8 = DIP SWITCH [package=dipswitch-02]
  R16 = Resistor [tolerance=±1% resistance=100 package=THT]
  R17 = Resistor [tolerance=±1% resistance=100 package=THT]
  R18 = Resistor [tolerance=±1% resistance=100 package=THT]
  SW9 = DIP SWITCH [package=dipswitch-02]
  SW10 = DIP SWITCH [package=dipswitch-02]
  R19 = Resistor [tolerance=±1% resistance=100 package=THT]
  R20 = Resistor [tolerance=±1% resistance=100 package=THT]
  U2 = POT [package=pot_alpha_rv16af-20]
  J1 = Camdenboss CTB0158-2 [part_number=CTB0158-2 package=THT]
  J2 = Power Jack [package=power_jack_pth_lock]
  S1 = SWITCH-MOMENTARY-2 [package=tactile-pth]

nets:
  N1: R1.Pin_0, SW1.1
  N2: R1.Pin_1, R2.Pin_1, R4.Pin_1, R3.Pin_1, R5.Pin_1, R6.Pin_1, R7.Pin_1, R8.Pin_1, R9.Pin_1, R10.Pin_1, R11.Pin_1, R12.Pin_1, R13.Pin_1, R14.Pin_1, R15.Pin_1, R16.Pin_1, R17.Pin_1, R18.Pin_1, R20.Pin_1, U2.S, J1.pin1, J2.GND, J2.GNDBREAK
  N3: SW1.2, R2.Pin_0
  N4: SW1.3, SW1.4, SW2.3, SW2.4, SW3.3, SW3.4, SW4.3, SW4.4, SW5.3, SW5.4, SW6.3, SW6.4, SW7.3, SW7.4, SW8.3, SW8.4, SW9.3, SW9.4, SW10.3, SW10.4, S1.2
  N5: R4.Pin_0, SW2.2
  N6: SW2.1, R3.Pin_0
  N7: R5.Pin_0, SW3.1
  N8: SW3.2, R6.Pin_0
  N9: SW4.1, R11.Pin_0
  N10: SW4.2, R7.Pin_0
  N11: R8.Pin_0, SW5.1
  N12: R9.Pin_0, SW5.2
  N13: R10.Pin_0, SW6.2
  N14: R12.Pin_0, SW6.1
  N15: SW7.1, R17.Pin_0
  N16: SW7.2, R13.Pin_0
  N17: R14.Pin_0, SW8.1
  N18: R15.Pin_0, SW8.2
  N19: R16.Pin_0, SW9.2
  N20: R18.Pin_0, SW9.1
  N21: SW10.1, R20.Pin_0
  N22: SW10.2, R19.Pin_0
  N23: R19.Pin_1, U2.A
  N24: J1.pin2, J2.PWR, S1.1
