# Fritzing sketch Fritzing_Schematic (saved by Fritzing 1.0.3b)
breadboards: 1

parts:
  Part1 = PTSolns Nano Flip V2.0 [mpn=PTS-00196-201 part_number=4272-PTS-00196-201-ND]
  ZS-042_RTC1 = ZS-042 RTC Module
  Driver1 = 28BYJ-48 Driver Module [part_number=ULN2003 package=THT]
  SM1 = 28BYJ-48 Stepper Motor [part_number=28BYJ-48]
  Q2 = Basic FET P-Channel [package="DPak [SMD]"]
  R1 = Resistor [tolerance=±5% resistance=220 package="2010 [SMD]"]
  R2 = Resistor [tolerance=±5% resistance=10k package="2010 [SMD]"]

nets:
  N1: Part1.A4, ZS-042_RTC1.SDA
  N2: Part1.A5, ZS-042_RTC1.SCL
  N3: Part1.D3, R1.Pin_1
  N4: Part1.D8, Driver1.IN1
  N5: Part1.D9, Driver1.IN2
  N6: Part1.D10, Driver1.IN3
  N7: Part1.D11, Driver1.IN4
  GND: ZS-042_RTC1.GND, Driver1.GND
  N8: ZS-042_RTC1.VCC, Q2.source, R2.Pin_0
  N9: Driver1.Vmotor, Q2.drain
  N10: Driver1.blue-pin, SM1.blue-pin
  N11: Driver1.pink-pin, SM1.pink-pin
  N12: Driver1.yellow-pin, SM1.yellow-pin
  N13: Driver1.orange-pin, SM1.orange-pin
  N14: Driver1.red-pin, SM1.red-pin
  N15: Q2.Gate, R1.Pin_0, R2.Pin_1

custom parts:
  PTSolns Nano Flip V2.0: Description The PTSolns Nano Flip is the modern twist on the classic Nano microcontroller. The popular ATmega328P microcontroller is embedded on the Nano Flip, providing all the features users come to expect. A large online community, tutorials, and support makes the Nano Flip a great choice in educational, hobby and professional settings for any project from getting started in the world of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
  28BYJ-48 Driver Module: ULN2003 Driver Module for the 28BYJ-48 Unipolar Stepper Motor LED A - Blue wire - Bottom coil left LED B - Pink wire - Top coil left LED C - Yellow wire - Bottom coil right LED D - Orange wire - Top coil right Common rail - red Connector pins: blue - pink - yellow - orange - red Control pins - IN1 to IN4 Power pins - GND & Vmotor (5-12V) On/Off jumper (if removed, power to motor is cut).
  28BYJ-48 Stepper Motor: Unipolar Stepper Motor 28BYJ-48 Top coil - pink & orange Bottom coil - blue & yellow Common rail - red Connector pins: blue - pink - yellow - orange - red
