# Fritzing sketch Nano_that_wants_to_be_an_Uno (saved by Fritzing 1.0.3b)

parts:
  Breadboard2 = PTSolns Proto-Shield V2.0 [mpn=PTS-00153-211 part_number=4272-PTS-00153-211-ND]
  Part1 = PTSolns Nano Flip V2.0 [mpn=PTS-00196-201 part_number=4272-PTS-00196-201-ND]
  S1 = Momentary Switch [package=ksa_sealed_tac_switch]
  Breadboard3 = PTSolns Proto-Shield V2.0 [mpn=PTS-00153-211 part_number=4272-PTS-00153-211-ND]

nets:
  N1: Breadboard2.connector3V3Dpin, Breadboard2.connectorJ7pin, Breadboard2.connectorL7pin, Part1.3V3
  N2: Breadboard2.connector5V1Apin, Breadboard2.connectorI17pin, Breadboard2.connectorJ17pin, Breadboard2.connectorW1pin, Breadboard2.connectorW17pin, Part1.5V
  N3: Breadboard2.connectorA0Bpin, Breadboard2.connectorJ9pin, Breadboard2.connectorL9pin, Part1.A0
  N4: Breadboard2.connectorA1Bpin, Breadboard2.connectorJ10pin, Breadboard2.connectorL10pin, Part1.A1
  N5: Breadboard2.connectorA2Bpin, Breadboard2.connectorJ11pin, Breadboard2.connectorL11pin, Part1.A2
  N6: Breadboard2.connectorA3Bpin, Breadboard2.connectorJ12pin, Breadboard2.connectorL12pin, Part1.A3
  N7: Breadboard2.connectorA4Bpin, Breadboard2.connectorJ13pin, Breadboard2.connectorK13pin, Breadboard2.connectorL13pin, Breadboard2.connectorSDACpin, Part1.A4
  N8: Breadboard2.connectorA5Bpin, Breadboard2.connectorJ14pin, Breadboard2.connectorK14pin, Breadboard2.connectorL14pin, Breadboard2.connectorSCLCpin, Part1.A5
  N9: Breadboard2.connectorAREFBpin, Breadboard2.connectorJ8pin, Breadboard2.connectorL8pin, Part1.REF
  N10: Breadboard2.connectorC4pin, Breadboard2.connectorI6pin, Breadboard2.connectorJ6pin, Breadboard2.connectorL6pin, Breadboard2.connectorSCKDpin, Part1.D13
  N11: Breadboard2.connectorC5pin, Breadboard2.connectorMISODpin, Breadboard2.connectorSOIC7Bpin, Breadboard2.connectorSOIC9Bpin, Breadboard2.connectorSOIC11Bpin, Part1.D12
  N12: Breadboard2.connectorC6pin, Breadboard2.connectorMOSIDpin, Breadboard2.connectorSOIC8Bpin, Breadboard2.connectorSOIC10Bpin, Breadboard2.connectorSOIC12Bpin, Part1.D11
  N13: Breadboard2.connectorC7pin, Breadboard2.connectorE8pin, Breadboard2.connectorF8pin, Part1.D10
  N14: Breadboard2.connectorC8pin, Breadboard2.connectorE9pin, Breadboard2.connectorF9pin, Part1.D9
  N15: Breadboard2.connectorC9pin, Breadboard2.connectorE10pin, Breadboard2.connectorF10pin, Part1.D8
  N16: Breadboard2.connectorC10pin, Breadboard2.connectorE11pin, Breadboard2.connectorF11pin, Part1.D7
  N17: Breadboard2.connectorC11pin, Breadboard2.connectorE12pin, Breadboard2.connectorF12pin, Part1.D6
  N18: Breadboard2.connectorC12pin, Breadboard2.connectorE13pin, Breadboard2.connectorF13pin, Part1.D5
  N19: Breadboard2.connectorC13pin, Breadboard2.connectorE14pin, Breadboard2.connectorF14pin, Part1.D4
  N20: Breadboard2.connectorC14pin, Breadboard2.connectorE15pin, Breadboard2.connectorF15pin, Part1.D3
  N21: Breadboard2.connectorC15pin, Breadboard2.connectorE16pin, Breadboard2.connectorF16pin, Part1.D2
  N22: Breadboard2.connectorC16pin, Breadboard2.connectorE19pin, Breadboard2.connectorF19pin, Part1.RX0
  N23: Breadboard2.connectorC17pin, Breadboard2.connectorE20pin, Breadboard2.connectorF20pin, Part1.TX1
  N24: Breadboard2.connectorF17pin, Part1.GND#19
  N25: Breadboard2.connectorF18pin, Part1.RST#18
  N26: Breadboard2.connectorGND1Dpin, Breadboard2.connectorGND2Epin, Breadboard2.connectorGND2Fpin, Breadboard2.connectorI4pin, Breadboard2.connectorI19pin, Breadboard2.connectorJ19pin, Breadboard2.connectorK4pin, Breadboard2.connectorL19pin, Breadboard2.connectorV1pin, Breadboard2.connectorV3pin, Breadboard2.connectorV18pin, Part1.GND#14, S1.3
  N27: Breadboard2.connectorJ15pin, Part1.A6
  N28: Breadboard2.connectorJ16pin, Part1.A7
  N29: Breadboard2.connectorJ18pin, Breadboard2.connectorK18pin, Breadboard2.connectorL18pin, Breadboard2.connectorRESETCpin, Breadboard2.connectorRSTBpin, Breadboard2.connectorX1pin, Breadboard2.connectorX4pin, Breadboard2.connectorX9pin, Breadboard2.connectorY1pin, Breadboard2.connectorY2pin, Part1.RST#13, S1.1, S1.2
  N30: Breadboard2.connectorJ20pin, Breadboard2.connectorL20pin, Breadboard2.connectorVINBpin, Part1.VIN
  N31: Breadboard2.connectorK1pin, S1.4
  N32: Breadboard3.connector3V3Dpin, Breadboard3.connectorL7pin
  N33: Breadboard3.connector5V1Apin, Breadboard3.connectorI17pin, Breadboard3.connectorW1pin, Breadboard3.connectorW17pin
  N34: Breadboard3.connectorA0Bpin, Breadboard3.connectorL9pin
  N35: Breadboard3.connectorA1Bpin, Breadboard3.connectorL10pin
  N36: Breadboard3.connectorA2Bpin, Breadboard3.connectorL11pin
  N37: Breadboard3.connectorA3Bpin, Breadboard3.connectorL12pin
  N38: Breadboard3.connectorA4Bpin, Breadboard3.connectorK13pin, Breadboard3.connectorL13pin, Breadboard3.connectorSDACpin
  N39: Breadboard3.connectorA5Bpin, Breadboard3.connectorK14pin, Breadboard3.connectorL14pin, Breadboard3.connectorSCLCpin
  N40: Breadboard3.connectorAREFBpin, Breadboard3.connectorL8pin
  N41: Breadboard3.connectorC5pin, Breadboard3.connectorSOIC7Bpin
  N42: Breadboard3.connectorC6pin, Breadboard3.connectorSOIC8Bpin
  N43: Breadboard3.connectorC7pin, Breadboard3.connectorE8pin
  N44: Breadboard3.connectorC8pin, Breadboard3.connectorE9pin
  N45: Breadboard3.connectorC9pin, Breadboard3.connectorE10pin
  N46: Breadboard3.connectorC10pin, Breadboard3.connectorE11pin
  N47: Breadboard3.connectorC11pin, Breadboard3.connectorE12pin
  N48: Breadboard3.connectorC12pin, Breadboard3.connectorE13pin
  N49: Breadboard3.connectorC13pin, Breadboard3.connectorE14pin
  N50: Breadboard3.connectorC14pin, Breadboard3.connectorE15pin
  N51: Breadboard3.connectorC15pin, Breadboard3.connectorE16pin
  N52: Breadboard3.connectorC16pin, Breadboard3.connectorE19pin
  N53: Breadboard3.connectorC17pin, Breadboard3.connectorE20pin
  N54: Breadboard3.connectorGND1Dpin, Breadboard3.connectorGND2Epin, Breadboard3.connectorGND2Fpin, Breadboard3.connectorI19pin, Breadboard3.connectorL19pin, Breadboard3.connectorV1pin, Breadboard3.connectorV18pin
  N55: Breadboard3.connectorI6pin, Breadboard3.connectorSCKDpin
  N56: Breadboard3.connectorK18pin, Breadboard3.connectorRESETCpin
  N57: Breadboard3.connectorL20pin, Breadboard3.connectorVINBpin
  N58: Breadboard3.connectorMISODpin, Breadboard3.connectorSOIC9Bpin, Breadboard3.connectorSOIC11Bpin
  N59: Breadboard3.connectorMOSIDpin, Breadboard3.connectorSOIC10Bpin, Breadboard3.connectorSOIC12Bpin

custom parts:
  PTSolns Proto-Shield V2.0: Description The PTSolns Proto-Shield Kit is a shield designed to enable the user to prototype their circuit as a shield. A unique prototyping section allows for much flexibility. Two configurable central power rails run across the entire length of the board. Above and below these rails are rows-of-four sections, mimicking the traditional breadboard layout. The board is fully stackable with all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
  PTSolns Nano Flip V2.0: Description The PTSolns Nano Flip is the modern twist on the classic Nano microcontroller. The popular ATmega328P microcontroller is embedded on the Nano Flip, providing all the features users come to expect. A large online community, tutorials, and support makes the Nano Flip a great choice in educational, hobby and professional settings for any project from getting started in the world of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
